// Logisim project SAP1 1607048.circ as structural Verilog: 9 circuits, main circuit main
module main (
  input  CLR,
  input  [3:0] HIGH,
  input  [3:0] LOW,
  input  Cin_SW_A_S_Su,
  output Cout,
  output Out7,
  output Out6,
  output Out5,
  output Out4,
  output Out3,
  output Out2,
  output Out1,
  output Out0
);

  wire CLK_out, controlled_buffer_1_out, controller_1_hlt, Cp, EA, Ep, EU, nCE, nEI, nL0, nLA, nLB, nLI, nLM,
       not_1_out, not_2_out, not_3_out, not_4_out, not_5_out, not_6_out, not_7_out, not_8_out, SU;
  wire [3:0] register_4_bit_1_y0, register_8_bit_1_y0, register_8_bit_1_y4;
  wire [7:0] alu_1_s, bit_extender_1_out, register_8_bit_2_y0, register_8_bit_3_y0, XOR_out;

  not not_1 (not_1_out, nLM);
  not not_2 (not_2_out, nCE);
  not not_3 (not_3_out, controller_1_hlt);
  Program_Counter program_counter_1 (
    .C3(LOW[3]), .C2(LOW[2]), .C1(LOW[1]), .C0(LOW[0]), .COUNT(Cp), .CLR(CLR), .CLK(controlled_buffer_1_out),
    .ENABLE(Ep));
  Register_4_bit register_4_bit_1 (
    .X3(LOW[3]), .X2(LOW[2]), .X1(LOW[1]), .X0(LOW[0]), .Y3(register_4_bit_1_y0[3]),
    .Y2(register_4_bit_1_y0[2]), .Y1(register_4_bit_1_y0[1]), .Y0(register_4_bit_1_y0[0]), .LOAD(not_1_out),
    .CLK(controlled_buffer_1_out), .CLR(CLR), .ENABLE(1'b1));
  RAM #(.addrWidth(4)) ram_1 (.addr(register_4_bit_1_y0), .data({HIGH, LOW}), .sel(not_2_out));  // open: clk, ld, clr
  Register_8_bit register_8_bit_1 (
    .X7(HIGH[3]), .X6(HIGH[2]), .X5(HIGH[1]), .X4(HIGH[0]), .X3(LOW[3]), .X2(LOW[2]), .X1(LOW[1]),
    .X0(LOW[0]), .Y7(register_8_bit_1_y4[3]), .Y6(register_8_bit_1_y4[2]), .Y5(register_8_bit_1_y4[1]),
    .Y4(register_8_bit_1_y4[0]), .Y3(register_8_bit_1_y0[3]), .Y2(register_8_bit_1_y0[2]),
    .Y1(register_8_bit_1_y0[1]), .Y0(register_8_bit_1_y0[0]), .LOAD(not_4_out),
    .CLK(controlled_buffer_1_out), .CLR(CLR), .ENABLE(1'b1));
  Controller controller_1 (
    .I7_I6_I5_I4(register_8_bit_1_y4), .HLT(controller_1_hlt), .Cp(Cp), .Ep(Ep), .nLM(nLM), .nCE(nCE),
    .nLi(nLI), .nEI(nEI), .nLA(nLA), .EA(EA), .SU(SU), .EU(EU), .nLB(nLB), .nL0(nL0),
    .CLK(controlled_buffer_1_out), .CLR(CLR));
  Clock CLK (.out(CLK_out));
  assign controlled_buffer_1_out = not_3_out ? CLK_out : 1'bz;  // Controlled_Buffer controlled_buffer_1
  not not_4 (not_4_out, nLI);
  assign LOW = not_5_out ? register_8_bit_1_y0 : 4'bz;  // Controlled_Buffer controlled_buffer_2
  not not_5 (not_5_out, nEI);
  not not_6 (not_6_out, nLA);
  Register_8_bit register_8_bit_2 (
    .X7(HIGH[3]), .X6(HIGH[2]), .X5(HIGH[1]), .X4(HIGH[0]), .X3(LOW[3]), .X2(LOW[2]), .X1(LOW[1]),
    .X0(LOW[0]), .Y7(register_8_bit_2_y0[7]), .Y6(register_8_bit_2_y0[6]), .Y5(register_8_bit_2_y0[5]),
    .Y4(register_8_bit_2_y0[4]), .Y3(register_8_bit_2_y0[3]), .Y2(register_8_bit_2_y0[2]),
    .Y1(register_8_bit_2_y0[1]), .Y0(register_8_bit_2_y0[0]), .LOAD(not_6_out),
    .CLK(controlled_buffer_1_out), .CLR(CLR), .ENABLE(1'b1));
  assign {HIGH, LOW} = EA ? register_8_bit_2_y0 : 8'bz;  // Controlled_Buffer controlled_buffer_3
  assign {HIGH, LOW} = EU ? alu_1_s : 8'bz;  // Controlled_Buffer controlled_buffer_4
  not not_7 (not_7_out, nLB);
  not not_8 (not_8_out, nL0);
  ALU alu_1 (.X(register_8_bit_2_y0), .Y(XOR_out), .Cin(Cin_SW_A_S_Su), .S(alu_1_s), .Cout(Cout));
  Register_8_bit register_8_bit_3 (
    .X7(HIGH[3]), .X6(HIGH[2]), .X5(HIGH[1]), .X4(HIGH[0]), .X3(LOW[3]), .X2(LOW[2]), .X1(LOW[1]),
    .X0(LOW[0]), .Y7(register_8_bit_3_y0[7]), .Y6(register_8_bit_3_y0[6]), .Y5(register_8_bit_3_y0[5]),
    .Y4(register_8_bit_3_y0[4]), .Y3(register_8_bit_3_y0[3]), .Y2(register_8_bit_3_y0[2]),
    .Y1(register_8_bit_3_y0[1]), .Y0(register_8_bit_3_y0[0]), .LOAD(not_7_out),
    .CLK(controlled_buffer_1_out), .CLR(CLR), .ENABLE(1'b1));
  Register_8_bit register_8_bit_4 (
    .X7(HIGH[3]), .X6(HIGH[2]), .X5(HIGH[1]), .X4(HIGH[0]), .X3(LOW[3]), .X2(LOW[2]), .X1(LOW[1]),
    .X0(LOW[0]), .Y7(Out7), .Y6(Out6), .Y5(Out5), .Y4(Out4), .Y3(Out3), .Y2(Out2), .Y1(Out1), .Y0(Out0),
    .LOAD(not_8_out), .CLK(controlled_buffer_1_out), .CLR(CLR), .ENABLE(1'b1));
  assign XOR_out = register_8_bit_3_y0 ^ bit_extender_1_out;  // XOR_Gate XOR, 8 bits wide
  assign bit_extender_1_out = {{7{Cin_SW_A_S_Su}}, Cin_SW_A_S_Su};  // Bit_Extender bit_extender_1
  Hex_Digit_Display hex_digit_display_1 (.value({Out7, Out6, Out5, Out4}));  // open: dp
  Hex_Digit_Display hex_digit_display_2 (.value({Out3, Out2, Out1, Out0}));  // open: dp

  // Notes on the sheet:
  //   Roll: 1607048
  //   Roll: 1607048
  //   IR
  //   ENABLE
  //   ADD/SUB
  //   A
  //   B
  //   OUT
  //   Roll: 1607048
  //   Roll: 1607048
  //   Roll: 1607048
endmodule

module FA (
  input  X,
  input  Y,
  input  Z,
  output S,
  output C
);

  wire AND_1_out, AND_2_out, XOR_1_out;

  xor XOR_1 (XOR_1_out, X, Y);
  and AND_1 (AND_1_out, X, Y);
  xor XOR_2 (S, XOR_1_out, Z);
  and AND_2 (AND_2_out, Z, XOR_1_out);
  or OR (C, AND_2_out, AND_1_out);

  // Notes on the sheet:
  //   Name: Faisal Ahmed
  //   Roll: 1607048
endmodule

// MAR
module Register_4_bit (
  input  X3,
  input  X2,
  input  X1,
  input  X0,
  input  LOAD,
  input  CLK,
  input  CLR,
  input  ENABLE,
  output Y3,
  output Y2,
  output Y1,
  output Y0
);

  wire and_1_out, and_2_out, and_3_out, and_4_out, and_5_out, and_6_out, and_7_out, and_8_out, d_ff_1_q,
       d_ff_2_q, d_ff_3_q, d_ff_4_q, not_1_out, or_1_out, or_2_out, or_3_out, or_4_out;

  and and_1 (and_1_out, d_ff_1_q, not_1_out);
  and and_2 (and_2_out, X3, LOAD);
  or or_1 (or_1_out, and_1_out, and_2_out);
  D_Flip_Flop d_ff_1 (.clk(CLK), .D(or_1_out), .Q(d_ff_1_q), .reset(CLR));  // open: Qn, preset, en
  assign Y3 = ENABLE ? d_ff_1_q : 1'bz;  // Controlled_Buffer controlled_buffer_1
  and and_3 (and_3_out, d_ff_2_q, not_1_out);
  or or_2 (or_2_out, and_3_out, and_4_out);
  and and_4 (and_4_out, X2, LOAD);
  D_Flip_Flop d_ff_2 (.clk(CLK), .D(or_2_out), .Q(d_ff_2_q), .reset(CLR));  // open: Qn, preset, en
  assign Y2 = ENABLE ? d_ff_2_q : 1'bz;  // Controlled_Buffer controlled_buffer_2
  buf and_5 (and_5_out, d_ff_3_q);  // AND_Gate
  or or_3 (or_3_out, and_5_out, and_6_out);
  and and_6 (and_6_out, X1, LOAD);
  D_Flip_Flop d_ff_3 (.clk(CLK), .D(or_3_out), .Q(d_ff_3_q), .reset(CLR));  // open: Qn, preset, en
  and and_7 (and_7_out, d_ff_4_q, not_1_out);
  assign Y1 = ENABLE ? d_ff_3_q : 1'bz;  // Controlled_Buffer controlled_buffer_3
  not not_1 (not_1_out, LOAD);
  and and_8 (and_8_out, X0, LOAD);
  or or_4 (or_4_out, and_7_out, and_8_out);
  D_Flip_Flop d_ff_4 (.clk(CLK), .D(or_4_out), .Q(d_ff_4_q), .reset(CLR));  // open: Qn, preset, en
  assign Y0 = ENABLE ? d_ff_4_q : 1'bz;  // Controlled_Buffer controlled_buffer_4

  // Notes on the sheet:
  //   Roll:1607048
endmodule

module Register_8_bit (
  input  X3,
  input  X2,
  input  X1,
  input  X0,
  input  X7,
  input  X6,
  input  X5,
  input  X4,
  input  LOAD,
  input  CLK,
  input  CLR,
  input  ENABLE,
  output Y3,
  output Y2,
  output Y1,
  output Y0,
  output Y5,
  output Y4,
  output Y7,
  output Y6
);

  wire and_1_out, and_2_out, and_3_out, and_4_out, and_5_out, and_6_out, and_7_out, and_8_out, and_9_out,
       and_10_out, and_11_out, and_12_out, and_13_out, and_14_out, and_15_out, and_16_out, d_ff_1_q,
       d_ff_2_q, d_ff_3_q, d_ff_4_q, d_ff_5_q, d_ff_6_q, d_ff_7_q, d_ff_8_q, not_1_out, or_1_out, or_2_out,
       or_3_out, or_4_out, or_5_out, or_6_out, or_7_out, or_8_out;

  and and_1 (and_1_out, d_ff_1_q, not_1_out);
  and and_2 (and_2_out, X7, LOAD);
  or or_1 (or_1_out, and_1_out, and_2_out);
  D_Flip_Flop d_ff_1 (.clk(CLK), .D(or_1_out), .Q(d_ff_1_q), .reset(CLR));  // open: Qn, preset, en
  assign Y7 = ENABLE ? d_ff_1_q : 1'bz;  // Controlled_Buffer controlled_buffer_1
  and and_3 (and_3_out, d_ff_2_q, not_1_out);
  or or_2 (or_2_out, and_3_out, and_4_out);
  and and_4 (and_4_out, X6, LOAD);
  D_Flip_Flop d_ff_2 (.clk(CLK), .D(or_2_out), .Q(d_ff_2_q), .reset(CLR));  // open: Qn, preset, en
  assign Y6 = ENABLE ? d_ff_2_q : 1'bz;  // Controlled_Buffer controlled_buffer_2
  and and_5 (and_5_out, d_ff_3_q, not_1_out);
  or or_3 (or_3_out, and_5_out, and_6_out);
  and and_6 (and_6_out, X5, LOAD);
  D_Flip_Flop d_ff_3 (.clk(CLK), .D(or_3_out), .Q(d_ff_3_q), .reset(CLR));  // open: Qn, preset, en
  and and_7 (and_7_out, d_ff_4_q, not_1_out);
  assign Y5 = ENABLE ? d_ff_3_q : 1'bz;  // Controlled_Buffer controlled_buffer_3
  and and_8 (and_8_out, X4, LOAD);
  or or_4 (or_4_out, and_7_out, and_8_out);
  D_Flip_Flop d_ff_4 (.clk(CLK), .D(or_4_out), .Q(d_ff_4_q), .reset(CLR));  // open: Qn, preset, en
  assign Y4 = ENABLE ? d_ff_4_q : 1'bz;  // Controlled_Buffer controlled_buffer_4
  and and_9 (and_9_out, d_ff_5_q, not_1_out);
  or or_5 (or_5_out, and_9_out, and_10_out);
  and and_10 (and_10_out, X3, LOAD);
  D_Flip_Flop d_ff_5 (.clk(CLK), .D(or_5_out), .Q(d_ff_5_q), .reset(CLR));  // open: Qn, preset, en
  assign Y3 = ENABLE ? d_ff_5_q : 1'bz;  // Controlled_Buffer controlled_buffer_5
  and and_11 (and_11_out, d_ff_6_q, not_1_out);
  or or_6 (or_6_out, and_11_out, and_12_out);
  and and_12 (and_12_out, X2, LOAD);
  D_Flip_Flop d_ff_6 (.clk(CLK), .D(or_6_out), .Q(d_ff_6_q), .reset(CLR));  // open: Qn, preset, en
  buf and_13 (and_13_out, d_ff_7_q);  // AND_Gate
  assign Y2 = ENABLE ? d_ff_6_q : 1'bz;  // Controlled_Buffer controlled_buffer_6
  and and_14 (and_14_out, X1, LOAD);
  or or_7 (or_7_out, and_13_out, and_14_out);
  D_Flip_Flop d_ff_7 (.clk(CLK), .D(or_7_out), .Q(d_ff_7_q), .reset(CLR));  // open: Qn, preset, en
  and and_15 (and_15_out, d_ff_8_q, not_1_out);
  assign Y1 = ENABLE ? d_ff_7_q : 1'bz;  // Controlled_Buffer controlled_buffer_7
  not not_1 (not_1_out, LOAD);
  and and_16 (and_16_out, X0, LOAD);
  or or_8 (or_8_out, and_15_out, and_16_out);
  D_Flip_Flop d_ff_8 (.clk(CLK), .D(or_8_out), .Q(d_ff_8_q), .reset(CLR));  // open: Qn, preset, en
  assign Y0 = ENABLE ? d_ff_8_q : 1'bz;  // Controlled_Buffer controlled_buffer_8

  // Notes on the sheet:
  //   Roll: 1607048
endmodule

module ALU (
  input  [7:0] X,
  input  [7:0] Y,
  input  Cin,
  output [7:0] S,
  output Cout
);

  wire fa_1_c, fa_2_c, fa_3_c, fa_4_c, fa_5_c, fa_6_c, fa_7_c;

  FA fa_1 (.X(X[0]), .Y(Y[0]), .Z(Cin), .S(S[0]), .C(fa_1_c));
  FA fa_2 (.X(X[1]), .Y(Y[1]), .Z(fa_1_c), .S(S[1]), .C(fa_2_c));
  FA fa_3 (.X(X[2]), .Y(Y[2]), .Z(fa_2_c), .S(S[2]), .C(fa_3_c));
  FA fa_4 (.X(X[3]), .Y(Y[3]), .Z(fa_3_c), .S(S[3]), .C(fa_4_c));
  FA fa_5 (.X(X[4]), .Y(Y[4]), .Z(fa_4_c), .S(S[4]), .C(fa_5_c));
  FA fa_6 (.X(X[5]), .Y(Y[5]), .Z(fa_5_c), .S(S[5]), .C(fa_6_c));
  FA fa_7 (.X(X[6]), .Y(Y[6]), .Z(fa_6_c), .S(S[6]), .C(fa_7_c));
  FA fa_8 (.X(X[7]), .Y(Y[7]), .Z(fa_7_c), .S(S[7]), .C(Cout));

  // Notes on the sheet:
  //   Faisal Ahmed
  //   Roll: 1607048
  //   X=4 (00000100)
  //   Y=8 (00001000)
endmodule

// PC
module Program_Counter (
  input  COUNT,
  input  CLR,
  input  CLK,
  input  ENABLE,
  output C3,
  output C2,
  output C1,
  output C0
);

  wire AND1_out, AND2_out, AND3_out, j_k_ff_1_q, j_k_ff_2_q, j_k_ff_3_q, j_k_ff_4_q;

  and AND3 (AND3_out, COUNT, AND2_out, j_k_ff_2_q);
  J_K_Flip_Flop j_k_ff_1 (.J(AND3_out), .clk(CLK), .K(AND3_out), .Q(j_k_ff_1_q), .reset(CLR));  // open: Qn, preset, en
  assign C3 = ENABLE ? j_k_ff_1_q : 1'bz;  // Controlled_Buffer controlled_buffer_1
  and AND2 (AND2_out, COUNT, AND1_out, j_k_ff_3_q);
  J_K_Flip_Flop j_k_ff_2 (.J(AND2_out), .clk(CLK), .K(AND2_out), .Q(j_k_ff_2_q), .reset(CLR));  // open: Qn, preset, en
  assign C2 = ENABLE ? j_k_ff_2_q : 1'bz;  // Controlled_Buffer controlled_buffer_2
  and AND1 (AND1_out, COUNT, j_k_ff_4_q);
  J_K_Flip_Flop j_k_ff_3 (.J(AND1_out), .clk(CLK), .K(AND1_out), .Q(j_k_ff_3_q), .reset(CLR));  // open: Qn, preset, en
  assign C1 = ENABLE ? j_k_ff_3_q : 1'bz;  // Controlled_Buffer controlled_buffer_3
  J_K_Flip_Flop j_k_ff_4 (.J(COUNT), .clk(CLK), .K(COUNT), .Q(j_k_ff_4_q), .reset(CLR));  // open: Qn, preset, en
  assign C0 = ENABLE ? j_k_ff_4_q : 1'bz;  // Controlled_Buffer controlled_buffer_4

  // Notes on the sheet:
  //   Faisal Ahmed
  //   Roll: 1607048
  //   Ripple Counter
  //   Program Counter
endmodule

// R Counter
module Ring_Counter (
  input  CLK,
  input  CLR,
  output T6,
  output T5,
  output T4,
  output T3,
  output T2,
  output T1
);

  wire j_k_ff_1_qn, j_k_ff_2_qn, j_k_ff_3_qn, j_k_ff_4_qn, j_k_ff_5_qn, j_k_ff_6_q;

  J_K_Flip_Flop j_k_ff_1 (
    .J(T5), .clk(CLK), .K(j_k_ff_2_qn), .Q(T6), .Qn(j_k_ff_1_qn), .reset(CLR));  // open: preset, en
  J_K_Flip_Flop j_k_ff_2 (
    .J(T4), .clk(CLK), .K(j_k_ff_3_qn), .Q(T5), .Qn(j_k_ff_2_qn), .reset(CLR));  // open: preset, en
  J_K_Flip_Flop j_k_ff_3 (
    .J(T3), .clk(CLK), .K(j_k_ff_4_qn), .Q(T4), .Qn(j_k_ff_3_qn), .reset(CLR));  // open: preset, en
  J_K_Flip_Flop j_k_ff_4 (
    .J(T2), .clk(CLK), .K(j_k_ff_5_qn), .Q(T3), .Qn(j_k_ff_4_qn), .reset(CLR));  // open: preset, en
  J_K_Flip_Flop j_k_ff_5 (
    .J(T1), .clk(CLK), .K(j_k_ff_6_q), .Q(T2), .Qn(j_k_ff_5_qn), .reset(CLR));  // open: preset, en
  J_K_Flip_Flop j_k_ff_6 (
    .J(j_k_ff_1_qn), .clk(CLK), .K(T6), .Q(j_k_ff_6_q), .Qn(T1), .reset(CLR));  // open: preset, en

  // Notes on the sheet:
  //   Faisal Ahmed
  //   Roll: 1607048
endmodule

module Decoder (
  input  I7,
  input  I6,
  input  I5,
  input  I4,
  output LDA,
  output ADD,
  output SUB,
  output OUT,
  output HALT
);

  wire and_1_out, and_2_out, and_3_out, and_4_out, and_5_out, not_1_out, not_2_out, not_3_out, not_4_out;

  not not_1 (not_1_out, I7);
  not not_2 (not_2_out, I6);
  not not_3 (not_3_out, I5);
  not not_4 (not_4_out, I4);
  and and_1 (and_1_out, not_1_out, not_2_out, not_3_out, not_4_out);
  and and_2 (and_2_out, not_1_out, not_2_out, not_3_out, I4);
  and and_3 (and_3_out, not_1_out, not_2_out, I5, not_4_out);
  and and_4 (and_4_out, I7, I6, I5, not_4_out);
  and and_5 (and_5_out, I7, I6, I5, I4);
  buf buffer_1 (LDA, and_1_out);
  buf buffer_2 (ADD, and_2_out);
  buf buffer_3 (SUB, and_3_out);
  buf buffer_4 (OUT, and_4_out);
  buf buffer_5 (HALT, and_5_out);

  // Notes on the sheet:
  //   Faisal Ahmed
  //   Roll: 1607048
endmodule

// CONTROLLER
module Controller (
  input  CLK,
  input  CLR,
  input  [3:0] I7_I6_I5_I4,
  output nLM,
  output nCE,
  output nLi,
  output nEI,
  output nLA,
  output EA,
  output SU,
  output EU,
  output nLB,
  output nL0,
  output HLT,
  output Cp,
  output Ep
);

  wire and_1_out, and_2_out, and_3_out, and_4_out, and_5_out, and_6_out, and_7_out, and_8_out, and_9_out,
       and_10_out, and_11_out, and_12_out, and_14_out, and_16_out, and_17_out, and_18_out, and_19_out,
       decoder_1_add, decoder_1_lda, decoder_1_out, decoder_1_sub, not_1_out, not_3_out, or_1_out, or_2_out,
       or_3_out, or_4_out, or_6_out, ring_counter_1_t3, ring_counter_1_t4, ring_counter_1_t5,
       ring_counter_1_t6;

  Decoder decoder_1 (
    .I7(I7_I6_I5_I4[3]), .I6(I7_I6_I5_I4[2]), .I5(I7_I6_I5_I4[1]), .I4(I7_I6_I5_I4[0]), .LDA(decoder_1_lda),
    .ADD(decoder_1_add), .SUB(decoder_1_sub), .OUT(decoder_1_out), .HALT(HLT));
  not not_1 (not_1_out, Ep);
  and and_1 (and_1_out, decoder_1_lda, ring_counter_1_t4);
  and and_2 (and_2_out, decoder_1_add, ring_counter_1_t4);
  and and_3 (and_3_out, decoder_1_sub, ring_counter_1_t4);
  or or_1 (or_1_out, not_1_out, and_1_out, and_2_out, and_3_out);
  not not_2 (nLM, or_1_out);
  not not_3 (not_3_out, ring_counter_1_t3);
  and and_4 (and_4_out, decoder_1_lda, ring_counter_1_t5);
  and and_5 (and_5_out, decoder_1_add, ring_counter_1_t5);
  and and_6 (and_6_out, decoder_1_sub, ring_counter_1_t5);
  or or_2 (or_2_out, not_3_out, and_4_out, and_5_out, and_6_out);
  not not_4 (nCE, or_2_out);
  Ring_Counter ring_counter_1 (
    .T6(ring_counter_1_t6), .T5(ring_counter_1_t5), .T4(ring_counter_1_t4), .T3(ring_counter_1_t3), .T2(Cp),
    .T1(Ep), .CLK(CLK), .CLR(CLR));
  not not_5 (nLi, ring_counter_1_t3);
  and and_7 (and_7_out, decoder_1_lda, ring_counter_1_t4);
  and and_8 (and_8_out, decoder_1_sub, ring_counter_1_t4);
  and and_9 (and_9_out, decoder_1_add, ring_counter_1_t4);
  or or_3 (or_3_out, and_7_out, and_9_out, and_8_out);
  not not_6 (nEI, or_3_out);
  and and_10 (and_10_out, decoder_1_lda, ring_counter_1_t6);
  and and_11 (and_11_out, decoder_1_sub, ring_counter_1_t6);
  and and_12 (and_12_out, decoder_1_add, ring_counter_1_t6);
  or or_4 (or_4_out, and_10_out, and_12_out, and_11_out);
  not not_7 (nLA, or_4_out);
  and and_13 (EA, decoder_1_out, ring_counter_1_t4);
  and and_14 (and_14_out, decoder_1_add, ring_counter_1_t6);
  and and_15 (SU, decoder_1_sub, ring_counter_1_t4);
  and and_16 (and_16_out, decoder_1_sub, ring_counter_1_t6);
  or or_5 (EU, and_14_out, and_16_out);
  and and_17 (and_17_out, decoder_1_sub, ring_counter_1_t5);
  and and_18 (and_18_out, decoder_1_add, ring_counter_1_t5);
  or or_6 (or_6_out, and_18_out, and_17_out);
  not not_8 (nLB, or_6_out);
  and and_19 (and_19_out, decoder_1_out, ring_counter_1_t4);
  not not_9 (nL0, and_19_out);

  // Notes on the sheet:
  //   Faisal Ahmed
  //   Roll: 1607048
  //   Roll: 1607048
endmodule
